// Logisim project lw4_D8421_6.circ as structural Verilog: 1 circuit, main circuit main
module main (
  input  [3:0] in_1,
  output [3:0] out_2
);

  wire and_3_out, and_4_out, and_5_out, and_6_out, not_1_out, not_2_out, not_3_out, not_4_out, not_5_out,
       not_6_out, not_7_out, not_8_out, not_9_out, not_10_out, not_11_out;

  // Probe on in_1
  // Probe on out_2
  not not_1 (not_1_out, in_1[3]);
  not not_2 (not_2_out, in_1[2]);
  and and_1 (out_2[3], not_1_out, not_2_out, in_1[1]);
  not not_3 (not_3_out, in_1[2]);
  not not_4 (not_4_out, in_1[1]);
  and and_2 (out_2[2], not_3_out, not_4_out);
  not not_5 (not_5_out, in_1[3]);
  not not_6 (not_6_out, in_1[2]);
  not not_7 (not_7_out, in_1[1]);
  not not_8 (not_8_out, in_1[3]);
  and and_3 (and_3_out, not_5_out, not_6_out, not_7_out);
  and and_4 (and_4_out, not_8_out, in_1[2], in_1[1]);
  or or_1 (out_2[1], and_3_out, and_4_out);
  not not_9 (not_9_out, in_1[2]);
  not not_10 (not_10_out, in_1[1]);
  not not_11 (not_11_out, in_1[3]);
  and and_5 (and_5_out, not_9_out, not_10_out, in_1[0]);
  and and_6 (and_6_out, not_11_out, in_1[0]);
  or or_2 (out_2[0], and_5_out, and_6_out);

  // Notes on the sheet:
  //   ABCD
endmodule
