// Logisim project lw4_ODS_3.circ as structural Verilog: 1 circuit, main circuit main
module main (
  input  [7:0] in_1,
  input  in_2,
  input  [7:0] in_3,
  output [7:0] out_4
);

  wire not_1_out, not_2_out, not_3_out, not_4_out, not_5_out, not_6_out, not_7_out, not_8_out, not_9_out,
       not_10_out, not_11_out, not_12_out, not_13_out, not_14_out, not_15_out, not_16_out, not_17_out,
       not_18_out, not_19_out, not_20_out, not_21_out, not_22_out, not_23_out, not_24_out, not_25_out,
       not_26_out, not_27_out, not_28_out, not_29_out, not_30_out, not_31_out, not_32_out, not_33_out,
       not_34_out, not_35_out, not_36_out, not_37_out, not_38_out, not_39_out, not_40_out, not_41_out,
       not_42_out, not_43_out, not_44_out, not_45_out, not_46_out, not_47_out, not_48_out, or_1_out,
       or_2_out, or_3_out, or_4_out, or_5_out, or_6_out, or_7_out, or_8_out, or_9_out, or_10_out, or_11_out,
       or_12_out, or_13_out, or_14_out, or_15_out, or_16_out, or_17_out, or_18_out, or_19_out, or_20_out,
       or_21_out, or_22_out, or_23_out, or_24_out, or_25_out, or_26_out, or_27_out, or_28_out, or_29_out,
       or_30_out, or_31_out, or_32_out, or_33_out, or_34_out, or_35_out, or_36_out, or_37_out, or_38_out,
       or_39_out, or_40_out, or_41_out, or_42_out, or_43_out, or_44_out, or_45_out, or_46_out, or_47_out,
       or_48_out, or_49_out, or_50_out, or_51_out, or_52_out, or_53_out, or_54_out, or_55_out, or_56_out,
       \С_2_out , \С_3_out , \С_4_out , \С_5_out , \С_6_out , \С_7_out , \С_out ;

  // Probe on in_1
  // Probe on out_4
  // Probe on in_3
  not not_1 (not_1_out, in_1[0]);
  not not_2 (not_2_out, in_3[0]);
  not not_3 (not_3_out, in_1[0]);
  not not_4 (not_4_out, in_2);
  not not_5 (not_5_out, in_3[0]);
  not not_6 (not_6_out, in_2);
  not not_7 (not_7_out, in_1[1]);
  not not_8 (not_8_out, in_3[1]);
  not not_9 (not_9_out, in_1[1]);
  not not_10 (not_10_out, \С_out );
  not not_11 (not_11_out, in_3[1]);
  not not_12 (not_12_out, \С_out );
  not not_13 (not_13_out, in_1[2]);
  not not_14 (not_14_out, in_3[2]);
  not not_15 (not_15_out, in_1[2]);
  not not_16 (not_16_out, \С_2_out );
  not not_17 (not_17_out, in_3[2]);
  not not_18 (not_18_out, \С_2_out );
  not not_19 (not_19_out, in_1[3]);
  not not_20 (not_20_out, in_3[3]);
  not not_21 (not_21_out, in_1[3]);
  not not_22 (not_22_out, \С_3_out );
  not not_23 (not_23_out, in_3[3]);
  not not_24 (not_24_out, \С_3_out );
  not not_25 (not_25_out, in_1[4]);
  not not_26 (not_26_out, in_3[4]);
  not not_27 (not_27_out, in_1[4]);
  not not_28 (not_28_out, \С_4_out );
  not not_29 (not_29_out, in_3[4]);
  not not_30 (not_30_out, \С_4_out );
  not not_31 (not_31_out, in_1[5]);
  not not_32 (not_32_out, in_3[5]);
  not not_33 (not_33_out, in_1[5]);
  not not_34 (not_34_out, \С_5_out );
  not not_35 (not_35_out, in_3[5]);
  not not_36 (not_36_out, \С_5_out );
  not not_37 (not_37_out, in_1[6]);
  not not_38 (not_38_out, in_3[6]);
  not not_39 (not_39_out, in_1[6]);
  not not_40 (not_40_out, \С_6_out );
  not not_41 (not_41_out, in_3[6]);
  not not_42 (not_42_out, \С_6_out );
  not not_43 (not_43_out, in_1[7]);
  not not_44 (not_44_out, in_3[7]);
  not not_45 (not_45_out, in_1[7]);
  not not_46 (not_46_out, \С_7_out );
  not not_47 (not_47_out, in_3[7]);
  not not_48 (not_48_out, \С_7_out );
  or or_1 (or_1_out, not_1_out, not_2_out, in_2);
  or or_2 (or_2_out, not_3_out, in_3[0], not_4_out);
  or or_3 (or_3_out, in_1[0], not_5_out, not_6_out);
  or or_4 (or_4_out, in_1[0], in_3[0], in_2);
  or or_5 (or_5_out, not_7_out, not_8_out, \С_out );
  or or_6 (or_6_out, not_9_out, in_3[1], not_10_out);
  or or_7 (or_7_out, in_1[1], not_11_out, not_12_out);
  or or_8 (or_8_out, in_1[1], in_3[1], \С_out );
  or or_9 (or_9_out, not_13_out, not_14_out, \С_2_out );
  or or_10 (or_10_out, not_15_out, in_3[2], not_16_out);
  or or_11 (or_11_out, in_1[2], not_17_out, not_18_out);
  or or_12 (or_12_out, in_1[2], in_3[2], \С_2_out );
  or or_13 (or_13_out, not_19_out, not_20_out, \С_3_out );
  or or_14 (or_14_out, not_21_out, in_3[3], not_22_out);
  or or_15 (or_15_out, in_1[3], not_23_out, not_24_out);
  or or_16 (or_16_out, in_1[3], in_3[3], \С_3_out );
  or or_17 (or_17_out, not_25_out, not_26_out, \С_4_out );
  or or_18 (or_18_out, not_27_out, in_3[4], not_28_out);
  or or_19 (or_19_out, in_1[4], not_29_out, not_30_out);
  or or_20 (or_20_out, in_1[4], in_3[4], \С_4_out );
  or or_21 (or_21_out, not_31_out, not_32_out, \С_5_out );
  or or_22 (or_22_out, not_33_out, in_3[5], not_34_out);
  or or_23 (or_23_out, in_1[5], not_35_out, not_36_out);
  or or_24 (or_24_out, in_1[5], in_3[5], \С_5_out );
  or or_25 (or_25_out, not_37_out, not_38_out, \С_6_out );
  or or_26 (or_26_out, not_39_out, in_3[6], not_40_out);
  or or_27 (or_27_out, in_1[6], not_41_out, not_42_out);
  or or_28 (or_28_out, in_1[6], in_3[6], \С_6_out );
  or or_29 (or_29_out, not_43_out, not_44_out, \С_7_out );
  or or_30 (or_30_out, not_45_out, in_3[7], not_46_out);
  or or_31 (or_31_out, in_1[7], not_47_out, not_48_out);
  or or_32 (or_32_out, in_1[7], in_3[7], \С_7_out );
  and S (out_4[0], or_1_out, or_2_out, or_3_out, or_4_out);
  and S_2 (out_4[1], or_5_out, or_6_out, or_7_out, or_8_out);
  and S_3 (out_4[2], or_9_out, or_10_out, or_11_out, or_12_out);
  and S_4 (out_4[3], or_13_out, or_14_out, or_15_out, or_16_out);
  and S_5 (out_4[4], or_17_out, or_18_out, or_19_out, or_20_out);
  and S_6 (out_4[5], or_21_out, or_22_out, or_23_out, or_24_out);
  and S_7 (out_4[6], or_25_out, or_26_out, or_27_out, or_28_out);
  and S_8 (out_4[7], or_29_out, or_30_out, or_31_out, or_32_out);
  or or_33 (or_33_out, in_1[0], in_3[0]);
  or or_34 (or_34_out, in_1[0], in_2);
  or or_35 (or_35_out, in_3[0], in_2);
  or or_36 (or_36_out, in_1[1], in_3[1]);
  or or_37 (or_37_out, in_1[1], \С_out );
  or or_38 (or_38_out, in_3[1], \С_out );
  or or_39 (or_39_out, in_1[2], in_3[2]);
  or or_40 (or_40_out, in_1[2], \С_2_out );
  or or_41 (or_41_out, in_3[2], \С_2_out );
  or or_42 (or_42_out, in_1[3], in_3[3]);
  or or_43 (or_43_out, in_1[3], \С_3_out );
  or or_44 (or_44_out, in_3[3], \С_3_out );
  or or_45 (or_45_out, in_1[4], in_3[4]);
  or or_46 (or_46_out, in_1[4], \С_4_out );
  or or_47 (or_47_out, in_3[4], \С_4_out );
  or or_48 (or_48_out, in_1[5], in_3[5]);
  or or_49 (or_49_out, in_1[5], \С_5_out );
  or or_50 (or_50_out, in_3[5], \С_5_out );
  or or_51 (or_51_out, in_1[6], in_3[6]);
  or or_52 (or_52_out, in_1[6], \С_6_out );
  or or_53 (or_53_out, in_3[6], \С_6_out );
  or or_54 (or_54_out, in_1[7], in_3[7]);
  or or_55 (or_55_out, in_1[7], \С_7_out );
  or or_56 (or_56_out, in_3[7], \С_7_out );
  and \u_С  (\С_out , or_33_out, or_34_out, or_35_out);
  and \u_С_2  (\С_2_out , or_36_out, or_37_out, or_38_out);
  and \u_С_3  (\С_3_out , or_39_out, or_40_out, or_41_out);
  and \u_С_4  (\С_4_out , or_42_out, or_43_out, or_44_out);
  and \u_С_5  (\С_5_out , or_45_out, or_46_out, or_47_out);
  and \u_С_6  (\С_6_out , or_48_out, or_49_out, or_50_out);
  and \u_С_7  (\С_7_out , or_51_out, or_52_out, or_53_out);
  // AND_Gate С_8 has open pins: in0=or_54_out, in1=or_55_out, in2=or_56_out, out=open

  // Notes on the sheet:
  //   A
  //   B
endmodule
